// Logisim project ex5.circ as structural Verilog: 5 circuits, main circuit rotr
module rotr (
  input  [15:0] A,
  input  [15:0] in_2,
  input  [3:0] B,
  output [15:0] Out1
);

  wire [15:1] undriven, undriven_2, undriven_3, undriven_4;

  rot8 rot8_1 (.in_1({undriven, B[3]}));  // open: out_2
  rot4 rot4_1 (.in_1({undriven_4, B[2]}));  // open: out_2
  rot2 rot2_1 (.in_1({undriven_2, B[1]}));  // open: out_2
  rot1 rot1_1 (.in_1({undriven_3, B[0]}));  // open: out_2
  // Pins of 1 and 16 bits meet at {undriven, B[3]}
  // Pins of 1 and 16 bits meet at {undriven_4, B[2]}
  // Pins of 1 and 16 bits meet at {undriven_2, B[1]}
  // Pins of 1 and 16 bits meet at {undriven_3, B[0]}

  // Notes on the sheet:
  //   PUT CIRCUITRY HERE
endmodule

module rot8 (
  input  [15:0] in_1,
  output [15:0] out_2
);


  assign out_2 = {in_1[7:0], in_1[15:8]};

  // Notes on the sheet:
  //   PUT CIRCUITRY HERE
endmodule

module rot4 (
  input  [15:0] in_1,
  output [15:0] out_2
);


  assign out_2 = {in_1[3:0], in_1[15:4]};

  // Notes on the sheet:
  //   PUT CIRCUITRY HERE
endmodule

module rot2 (
  input  [15:0] in_1,
  output [15:0] out_2
);


  assign out_2 = {in_1[1:0], in_1[15:2]};

  // Notes on the sheet:
  //   PUT CIRCUITRY HERE
endmodule

module rot1 (
  input  [15:0] in_1,
  output [15:0] out_2
);


  assign out_2 = {in_1[0], in_1[15:1]};

  // Notes on the sheet:
  //   PUT CIRCUITRY HERE
endmodule
