// Logisim project ex5.circ as structural Verilog: 6 circuits, main circuit rotr
module rotr (
  input  [15:0] A,
  input  [3:0] B,
  output [15:0] Out1
);

  wire [15:0] rot1_2_out_2, rot1_3_out_2, rot1_4_out_2, rot1_5_out_2, rot1_6_out_2, rot1_7_out_2,
       rot1_8_out_2, rot2_1_out_2, rot2_2_out_2, rot2_3_out_2, rot2_5_out_2, rot2_6_out_2, rot2_7_out_2,
       rot2_8_out_2, rot4_1_out_2, rot4_2_out_2, rot4_3_out_2, rot4_4_out_2, rot4_5_out_2, rot4_6_out_2,
       rot4_7_out_2, rot4_8_out_2, rot4_9_out_2, rot4_10_out_2, rot4_11_out_2, rot4_12_out_2, rot4_13_out_2,
       rot4_14_out_2, rot8_1_out_2, rot8_2_out_2, rot8_3_out_2, rot8_4_out_2, rot8_5_out_2;

  rot8 rot8_1 (.in_1(A), .out_2(rot8_1_out_2));
  rot1 rot1_1 (.in_1(A));  // open: out_2
  rot4 rot4_1 (.in_1(A), .out_2(rot4_1_out_2));
  rot4 rot4_2 (.in_1(A), .out_2(rot4_2_out_2));
  rot8 rot8_2 (.in_1(A), .out_2(rot8_2_out_2));
  rot8 rot8_3 (.in_1(A), .out_2(rot8_3_out_2));
  rot8 rot8_4 (.in_1(A), .out_2(rot8_4_out_2));
  rot8 rot8_5 (.in_1(A), .out_2(rot8_5_out_2));
  rot4 rot4_3 (.in_1(rot8_1_out_2), .out_2(rot4_3_out_2));
  rot1 rot1_2 (.in_1(A), .out_2(rot1_2_out_2));
  rot2 rot2_1 (.in_1(A), .out_2(rot2_1_out_2));
  rot1 rot1_3 (.in_1(A), .out_2(rot1_3_out_2));
  rot2 rot2_2 (.in_1(rot1_3_out_2), .out_2(rot2_2_out_2));
  rot4 rot4_4 (.in_1(A), .out_2(rot4_4_out_2));
  rot1 rot1_4 (.in_1(A), .out_2(rot1_4_out_2));
  rot2 rot2_3 (.in_1(A), .out_2(rot2_3_out_2));
  rot2 rot2_4 ();  // open: in_1, out_2
  rot4 rot4_5 (.in_1(A), .out_2(rot4_5_out_2));
  rot4 rot4_6 (.in_1(rot4_1_out_2), .out_2(rot4_6_out_2));
  rot4 rot4_7 (.in_1(rot4_2_out_2), .out_2(rot4_7_out_2));
  rot2 rot2_5 (.in_1(rot8_2_out_2), .out_2(rot2_5_out_2));
  rot4 rot4_8 (.in_1(rot8_3_out_2), .out_2(rot4_8_out_2));
  rot4 rot4_9 (.in_1(rot8_4_out_2), .out_2(rot4_9_out_2));
  rot1 rot1_5 (.in_1(rot4_9_out_2), .out_2(rot1_5_out_2));
  rot4 rot4_10 (.in_1(rot8_5_out_2), .out_2(rot4_10_out_2));
  rot2 rot2_6 (.in_1(rot4_10_out_2), .out_2(rot2_6_out_2));
  rot2 rot2_7 (.in_1(rot4_3_out_2), .out_2(rot2_7_out_2));
  rot4 rot4_11 (.in_1(rot1_4_out_2), .out_2(rot4_11_out_2));
  rot4 rot4_12 (.in_1(rot2_3_out_2), .out_2(rot4_12_out_2));
  rot4 rot4_13 (.out_2(rot4_13_out_2));  // open: in_1
  rot4 rot4_14 (.in_1(rot4_5_out_2), .out_2(rot4_14_out_2));
  rot1 rot1_6 (.in_1(rot4_6_out_2), .out_2(rot1_6_out_2));
  rot2 rot2_8 (.in_1(rot4_7_out_2), .out_2(rot2_8_out_2));
  rot1 rot1_7 (.in_1(rot2_5_out_2), .out_2(rot1_7_out_2));
  rot1 rot1_8 (.in_1(rot2_7_out_2), .out_2(rot1_8_out_2));
  Multiplexer #(.select(4), .width(16), .enable("false")) multiplexer_1 (
    .in0(A), .in1(rot1_2_out_2), .in2(rot2_1_out_2), .in3(rot2_2_out_2), .in4(rot4_4_out_2),
    .in5(rot4_11_out_2), .in6(rot4_12_out_2), .in7(rot4_13_out_2), .in8(rot4_14_out_2), .in9(rot1_6_out_2),
    .in10(rot2_8_out_2), .in11(rot1_7_out_2), .in12(rot4_8_out_2), .in13(rot1_5_out_2), .in14(rot2_6_out_2),
    .in15(rot1_8_out_2), .out(Out1), .sel(B));

  // Notes on the sheet:
  //   PUT CIRCUITRY HERE
endmodule

module rot8 (
  input  [15:0] in_1,
  output [15:0] out_2
);


  assign out_2 = {in_1[7:0], in_1[15:8]};

  // Notes on the sheet:
  //   PUT CIRCUITRY HERE
endmodule

module rot4 (
  input  [15:0] in_1,
  output [15:0] out_2
);


  assign out_2 = {in_1[3:0], in_1[15:4]};

  // Notes on the sheet:
  //   PUT CIRCUITRY HERE
endmodule

module rot2 (
  input  [15:0] in_1,
  output [15:0] out_2
);


  assign out_2 = {in_1[1:0], in_1[15:2]};

  // Notes on the sheet:
  //   PUT CIRCUITRY HERE
endmodule

module rot1 (
  input  [15:0] in_1,
  output [15:0] out_2
);


  assign out_2 = {in_1[0], in_1[15:1]};

  // Notes on the sheet:
  //   PUT CIRCUITRY HERE
endmodule

module test1 (
  input  [3:0] in_1,
  input  [1:0] in_2,
  input  [1:0] in_3,
  input  in_4,
  input  [1:0] in_5,
  output out_6,
  output [1:0] out_7,
  output out_8,
  output out_9,
  output out_10,
  output out_11
);

  Bit_Extender #(.in_width(4), .out_width(1), .\type ("one")) bit_extender_1 (.in(in_1), .out(out_6));
  Multiplexer #(.width(2), .enable("false")) multiplexer_1 (.in0(in_2), .in1(in_3), .out(out_7), .sel(in_4));
  Decoder #(.select(2), .enable("false")) decoder_1 (
    .out0(out_8), .out1(out_9), .out2(out_10), .out3(out_11), .sel(in_5));
endmodule
